# Fritzing sketch Sketch Rangkaian (saved by Fritzing 0.9.5d)
perfboards: 6

parts:
  U = 4-Channel 5v Relay Shield [package=relay-4ch5v10a]
  Part2 = BH1750
  A1 = DFR0379
  esp1 = ESP32 DevKitc V4
  DHT1 = DHT22 Humidity and Temperature Sensor
  part = Fan - Ventilador [package=THT]
  A2 = RGB Strip LED
  A3 = S-350-60 Power Supply [part_number=S-350-60 package=THT]
  220_V = AC Power [voltage=12V frequency=60Hz]
  Pompa_Air = water pump/motor
  J1 = Camdenboss CTB0158-2 [part_number=CTB0158-2 package=THT]
  D1 = Rectifier Diode [part_number=1N5400 package="300 mil [THT]"]

nets:
  VCC: U.VCC, A1.Pin_7, A1.Pin_8, esp1.5V
  N1: U.GND, A1.Pin_4, A1.Pin_5, A1.Pin_6, esp1.GND#18, A2.Green_Connect, A3.-V1, A3.-V2, A3.-V3, Pompa_Air.pin_1, D1.anode
  N2: U.IN1, esp1.IO26
  N3: U.IN2, esp1.IO27
  N4: U.K1-In, J1.terminal_1
  N5: U.K1-On, U.K2-On, U.K3-On, U.K4-On, part.5V, A2.Common_Connect, Pompa_Air.pin_2, D1.cathode
  N6: U.K2-In, U.K3-In, A1.Pin_1, A1.Pin_2, A3.+V1, A3.+V2, A3.+V3, 220_V.V-
  N7: U.IN3, esp1.IO25
  N8: Part2.SCL, esp1.IO22
  N9: Part2.SDA, esp1.IO21
  N10: esp1.IO4, DHT1.DATA
  3V3: esp1.3V3, DHT1.VDD
  N11: part.GND, A3.N, J1.terminal_2
  N12: A3.L, J1.pin1

custom parts:
  4-Channel 5v Relay Shield: 4 Channel 5v Relay Shield w. 2x SPD-06VDC-SD-C
  BH1750: Light Sensor
  DFR0379: 20W Adjustable DC-DC Buck Converter with Digital Display.
  ESP32 DevKitc V4: ESP32-DevKitC board with ESP32-WROOM-32 module. ESP32-DevKitC V4 is a small-sized ESP32-based development board produced by Espressif. Most of the pins on the ESP module are broken out to the pin headers on the board. The pins D0, D1, D2, D3, CMD and CLK are used internally for communication between ESP32 and SPI flash memory. They are grouped on both sides near the USB connector. Avoid using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
  Fan - Ventilador: Ventilador de 2 pines, se encuentra comunmente en computadoras de escritorio
  RGB Strip LED: A tri-color Strip LED with red, green and blue. Pin order: red - common cathode - blue - green
  S-350-60 Power Supply: 350W Stepper motor power supply. June 2024 clean up errors in the part.
  water pump/motor: WATER PUMP BY ARDUBLOCKTR
  Rectifier Diode: A standard rectifier diode 1N5400 Note: this part contains several types of diode. Drag the part in to the sketch and Inspector will let you choose among: rectifier (1n4001) 300 mil, the P 1000K 10 A rectifier in seveal foot prints, a Schottky diode the 1n5817, a Zener diode the 1n4732A (and Inspector will let you change the zener voltage) and a Small signal diode (the 1n4148) in a variety of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
